# Fritzing sketch Master (saved by Fritzing 0.9.3b)
breadboards: 1

parts:
  M1 = TP4056 Module [part_number=HW-107]
  NodeMCU_v1 = NodeMCU v3 LoLin [part_number=ESP8266]
  R1 = Resistor [tolerance=±5% resistance=100k package="1206 [SMD]"]
  R2 = Resistor [tolerance=±5% resistance=100k package="1206 [SMD]"]
  U1 = LIPO-1000mAh [package=lipo-1000]
  SD_card_module3 = SD Card Module
  ZS-042_RTC1 = ZS-042 RTC Module
  Step_up1 = mini boost module
  F2 = Fan - Ventilador [package=THT]
  U3 = POT [package=pot_mammoth]

nets:
  N1: M1.OUT-#1, NodeMCU_v1.GND, R1.Pin_0, Step_up1.Pin_2
  N2: M1.BAT-, U1.-
  N3: M1.BAT+, U1.+
  N4: M1.OUT-#4, NodeMCU_v1.VIN, R2.Pin_0
  N5: NodeMCU_v1.D3, ZS-042_RTC1.SDA
  N6: NodeMCU_v1.D4, ZS-042_RTC1.SCL
  N7: NodeMCU_v1.D5, SD_card_module3.CS
  N8: NodeMCU_v1.D6, SD_card_module3.MOSI
  N9: NodeMCU_v1.D7, SD_card_module3.SCK
  N10: NodeMCU_v1.D8, SD_card_module3.MISO
  N11: NodeMCU_v1.A0, R1.Pin_1, R2.Pin_1
  N12: Step_up1.Pin_3, F2.GND
  N13: Step_up1.Pin_4, U3.S
  N14: F2.5V, U3.A

notes:
  Input: 4v
  Output: 12v
  Ingresso
  Input: 5v
  Output: 4v

custom parts:
  TP4056 Module: TP4056 Lithium Battery Charge Management Module Links: TP4056 website
  NodeMCU v3 LoLin: NodeMCU v3 LoLin NodeMCU (http://www.nodemcu.com/) is an open source IoT platform. It includes firmware (https://nodemcu-build.com/) which runs on the ESP8266 Wi-Fi SoC from Espressif Systems, and hardware which is based on the ESP-12E module. The term "NodeMCU" by default refers to the firmware rather than the dev kits. The firmware uses the Lua scripting language. It is based on the eLua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
  SD Card Module: SD Card Module Slot Socket Reader For Arduino ARM MCU
  mini boost module: mini boost module.
  Fan - Ventilador: Ventilador de 2 pines, se encuentra comunmente en computadoras de escritorio
