# Fritzing sketch Slave (saved by Fritzing 0.9.3b)
breadboards: 1

parts:
  WATER_PUMP1 = water pump/motor
  KY-1 = Keyes Relay [package=THT]
  U4 = POT [package=pot_mammoth]
  M2 = TP4056 Module [part_number=HW-107]
  NodeMCU_v2 = NodeMCU v3 LoLin [part_number=ESP8266]
  U5 = LIPO-1000mAh [package=lipo-1000]
  Step_up2 = mini boost module
  F3 = Fan - Ventilador [package=THT]
  Componente3 = Arduino Uno (Rev3) - ICSP
  Step_down5 = LM2596 step down module
  JACK1 = 2.1mm Barrel Jack with Terminal Block
  R28 = Resistor [tolerance=±5% resistance=100k package=THT]
  R29 = Resistor [tolerance=±5% resistance=100k package=THT]
  DHT5 = DHT22 Humidity and Temperature Sensor
  R37 = Resistor [tolerance=±5% resistance=47k package="2512 [SMD]"]
  R38 = PHOTOCELL [package=photocell-kit]
  R39 = Resistor [tolerance=±5% resistance=220 package="0805 [SMD]"]
  부품13 = FC-28 Soil Hygrometer Module - Probe
  부품14 = FC-28 Soil Hygrometer Module
  ZS-042_RTC2 = ZS-042 RTC Module
  SD_card_module4 = SD Card Module
  Water_Level_Sensor3 = Water Level Sensor
  R40 = Resistor [tolerance=±5% resistance=1k package=THT]
  R41 = Resistor [tolerance=±5% resistance=2k package="1206 [SMD]"]

nets:
  GND: WATER_PUMP1.pin_1, KY-1.power, Componente3.GND, DHT5.GND, R38.P$1, 부품14.GND, ZS-042_RTC2.GND, Water_Level_Sensor3.GND, R41.Pin_0
  N1: WATER_PUMP1.pin_2, KY-1.C
  VCC: KY-1.signal, KY-1.NO, Componente3.5V, DHT5.VDD, R39.Pin_1, 부품14.VCC, ZS-042_RTC2.VCC, Water_Level_Sensor3.VCC
  N2: KY-1.ground, Componente3.D13/SCK
  N3: U4.S, Step_up2.Pin_4, Step_down5.IN+
  N4: U4.A, F3.5V
  GND_2: M2.OUT-, NodeMCU_v2.GND, NodeMCU_v2.VIN, Step_up2.Pin_2, R28.Pin_0
  N5: M2.BAT-, U5.-
  N6: M2.BAT+, U5.+
  N7: NodeMCU_v2.RX, R40.Pin_1, R41.Pin_1
  N8: NodeMCU_v2.TX, Componente3.D7
  N9: Step_up2.Pin_3, F3.GND, Step_down5.IN-, Step_down5.OUT-, JACK1.NEG
  N10: Componente3.A0, R28.Pin_1, R29.Pin_1
  N11: Componente3.A1, 부품14.AO
  N12: Componente3.A2, R38.P$2, R39.Pin_0
  N13: Componente3.A3, Water_Level_Sensor3.SIG
  N14: Componente3.A4/SDA, ZS-042_RTC2.SDA
  N15: Componente3.A5/SCL, ZS-042_RTC2.SCL
  N16: Componente3.D12/MISO, R37.Pin_0
  N17: Componente3.D2, SD_card_module4.MISO
  N18: Componente3.D3_PWM, SD_card_module4.SCK
  N19: Componente3.D4, SD_card_module4.MOSI
  N20: Componente3.D5_PWM, SD_card_module4.CS
  N21: Componente3.D6_PWM, R40.Pin_0
  N22: Step_down5.OUT+, JACK1.POS
  N23: DHT5.DATA, R37.Pin_1
  N24: 부품13.POS, 부품14.POS
  N25: 부품13.NEG, 부품14.NEG

notes:
  Ingresso
  Input: 5v
  Output: 4v
  Input: 4v
  Output: 12v
  Input: 12v
  Output: 7v

custom parts:
  water pump/motor: WATER PUMP BY ARDUBLOCKTR
  Keyes Relay: The Keyes 5V relay module is suitable for SCM development, home appliance control. It uses a 5V~12V TIL control signal which can control DC / AC signal.
  TP4056 Module: TP4056 Lithium Battery Charge Management Module Links: TP4056 website
  NodeMCU v3 LoLin: NodeMCU v3 LoLin NodeMCU (http://www.nodemcu.com/) is an open source IoT platform. It includes firmware (https://nodemcu-build.com/) which runs on the ESP8266 Wi-Fi SoC from Espressif Systems, and hardware which is based on the ESP-12E module. The term "NodeMCU" by default refers to the firmware rather than the dev kits. The firmware uses the Lua scripting language. It is based on the eLua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
  mini boost module: mini boost module.
  Fan - Ventilador: Ventilador de 2 pines, se encuentra comunmente en computadoras de escritorio
  LM2596 step down module: LM2596 DC-DC step down power supply module 3 A.
  FC-28 Soil Hygrometer Module - Probe: The FC-28 is a soil hygrometer module that uses the Texas Instruments LM393 comparator chip to provide an analog measurement of soil humidity.
  FC-28 Soil Hygrometer Module: The FC-28 is a soil hygrometer module that uses the Texas Instruments LM393 comparator chip to provide an analog measurement of soil humidity. The digital output is high when soil moisture is over a certain threshold, as determined by adjusting the potentiometer.
  SD Card Module: SD Card Module Slot Socket Reader For Arduino ARM MCU
  Water Level Sensor: A water level sensor. This sensor operates at 3V to 5V. The Sig (signal) pin outputs an analogue signal that is in proportion to the amount of water in contact with the sensor.
